# Fritzing sketch SmartFarm (saved by Fritzing 0.9.3b)
breadboards: 2

parts:
  Componente1 = Arduino Uno (Rev3) - ICSP
  LED2 = LEDs [package=led10mm]
  R5 = Resistor [tolerance=±5% resistance=220 package=THT]
  R1 = Photocell (LDR) [package=THT]
  R7 = Resistor [tolerance=±5% resistance=220 package=THT]
  Q5 = NPN-Transistor [package="TO92 [THT]"]
  R8 = Resistor [tolerance=±5% resistance=220 package=THT]
  R9 = Photocell (LDR) [package=THT]
  R10 = Resistor [tolerance=±5% resistance=220 package=THT]
  R11 = Resistor [tolerance=±5% resistance=220 package=THT]
  R12 = Photocell (LDR) [package=THT]
  R13 = Resistor [tolerance=±5% resistance=220 package=THT]
  LED5 = LEDs [package=led10mm]
  Q6 = NPN-Transistor [package="TO92 [THT]"]
  LED6 = LEDs [package=led10mm]
  Q7 = NPN-Transistor [package="TO92 [THT]"]
  LED7 = LEDs [package=led10mm]
  Componente2 = Photon
  S1 = Round Pushbutton
  Componente3 = Photon
  Componente4 = Photon
  R14 = Resistor [tolerance=±5% resistance=220 package=THT]
  Q8 = NPN-Transistor [package="TO92 [THT]"]
  R15 = Resistor [tolerance=±5% resistance=220 package=THT]

nets:
  N1: Componente1.A2, R10.Pin_1
  N2: Componente1.A3, R7.Pin_1
  N3: Componente1.A4/SDA, R13.Pin_1
  N4: Componente1.D9_PWM, Q8.B
  N5: Componente1.D10_PWM/SS, R5.Pin_0
  GND: Componente1.GND, Q5.C, Q6.C, Q7.C, Componente2.VIN, Componente2.VBAT, Componente3.VIN, Componente3.VBAT, Componente4.GND, Q8.C, R15.Pin_1
  GND_2: Componente1.D2, Componente2.GND, Componente3.GND, Componente4.TX, Componente4.D7
  N6: Componente1.D3_PWM, Componente2.TX, Componente3.TX, Componente4.RX
  N7: Componente1.D5_PWM, R8.Pin_0
  N8: Componente1.D6_PWM, R11.Pin_0
  N9: Componente1.D7, S1.leg1, R15.Pin_0
  N10: Componente1.5V, R1.pin_0
  N11: LED2.C, Q5.B
  N12: LED2.A, LED5.A, LED6.A, LED7.A, S1.leg0
  N13: R5.Pin_1, Q5.E
  N14: R1.pin_1, R7.Pin_0
  N15: R8.Pin_1, Q6.E
  N16: R9.pin_1, R10.Pin_0
  N17: R11.Pin_1, Q7.E
  N18: R12.pin_1, R13.Pin_0
  N19: LED5.C, Q6.B
  N20: LED6.C, Q7.B
  N21: Componente2.A0, Componente3.A0
  N22: Componente2.A1, Componente3.A1, Componente4.A0
  N23: Componente2.A2, Componente3.A2, Componente4.A1
  N24: Componente2.A3, Componente3.A3, Componente4.A2
  N25: Componente2.A4, Componente3.A4, Componente4.A3
  N26: Componente2.A5, Componente3.A5, Componente4.A4
  N27: Componente2.DAC, Componente3.DAC, Componente4.A5
  N28: Componente2.WKP, Componente3.WKP, Componente4.DAC
  N29: Componente2.RX, Componente3.RX, Componente4.WKP
  N30: Componente2.D0, Componente3.D0
  N31: Componente2.D1, Componente3.D1, Componente4.D0
  N32: Componente2.D2, Componente3.D2, Componente4.D1
  N33: Componente2.D3, Componente3.D3, Componente4.D2
  N34: Componente2.D4, Componente3.D4, Componente4.D3
  N35: Componente2.D5, Componente3.D5, Componente4.D4
  N36: Componente2.D6, Componente3.D6, Componente4.D5
  N37: Componente2.D7, Componente3.D7, Componente4.D6
  N38: Componente2.RST, Componente3.RST, Componente4.VBAT
  3V3: Componente2.3V3, Componente3.3V3, Componente4.RST
  N39: R14.Pin_1, Q8.E

notes:
  Fuente 12V
